# Fritzing sketch Shiftregister (saved by Fritzing 0.9.3b)
circuit board: 9.05621cm x 10.5175cm
stripboards: 1

parts:
  U1 = 74HC595 [package="DIP16 [THT]"]
  R1 = Resistor [tolerance=±5% resistance=220 package=THT]
  R2 = Resistor [tolerance=±5% resistance=220 package=THT]
  R3 = Resistor [tolerance=±5% resistance=220 package=THT]
  R4 = Resistor [tolerance=±5% resistance=220 package=THT]
  R5 = Resistor [tolerance=±5% resistance=220 package=THT]
  R6 = Resistor [tolerance=±5% resistance=220 package=THT]
  R7 = Resistor [tolerance=±5% resistance=220 package=THT]
  R8 = Resistor [tolerance=±5% resistance=220 package=THT]
  U2 = 74HC595 [package="DIP16 [THT]"]
  R9 = Resistor [tolerance=±5% resistance=220 package=THT]
  R10 = Resistor [tolerance=±5% resistance=220 package=THT]
  R11 = Resistor [tolerance=±5% resistance=220 package=THT]
  R12 = Resistor [tolerance=±5% resistance=220 package=THT]
  R13 = Resistor [tolerance=±5% resistance=220 package=THT]
  R14 = Resistor [tolerance=±5% resistance=220 package=THT]
  R15 = Resistor [tolerance=±5% resistance=220 package=THT]
  R16 = Resistor [tolerance=±5% resistance=220 package=THT]
  J1 = shrouded pin header, 10 pins [form="♂ (shrouded male)"]
  U3 = 74HC595 [package="DIP16 [THT]"]
  R17 = Resistor [tolerance=±5% resistance=220 package=THT]
  R18 = Resistor [tolerance=±5% resistance=220 package=THT]
  R19 = Resistor [tolerance=±5% resistance=220 package=THT]
  R20 = Resistor [tolerance=±5% resistance=220 package=THT]
  R21 = Resistor [tolerance=±5% resistance=220 package=THT]
  R22 = Resistor [tolerance=±5% resistance=220 package=THT]
  R23 = Resistor [tolerance=±5% resistance=220 package=THT]
  R24 = Resistor [tolerance=±5% resistance=220 package=THT]
  U4 = 74HC595 [package="DIP16 [THT]"]
  R25 = Resistor [tolerance=±5% resistance=220 package=THT]
  R26 = Resistor [tolerance=±5% resistance=220 package=THT]
  R27 = Resistor [tolerance=±5% resistance=220 package=THT]
  R28 = Resistor [tolerance=±5% resistance=220 package=THT]
  R29 = Resistor [tolerance=±5% resistance=220 package=THT]
  R30 = Resistor [tolerance=±5% resistance=220 package=THT]
  R31 = Resistor [tolerance=±5% resistance=220 package=THT]
  R32 = Resistor [tolerance=±5% resistance=220 package=THT]
  J2 = shrouded pin header, 10 pins [form="♂ (shrouded male)"]
  J3 = shrouded pin header, 10 pins [form="♂ (shrouded male)"]
  J4 = shrouded pin header, 10 pins [form="♂ (shrouded male)"]
  J5 = shrouded pin header, 10 pins [form="♂ (shrouded male)"]

nets:
  N1: U1.Q1, R1.Pin_1
  N2: U1.Q2, R2.Pin_1
  N3: U1.Q3, R3.Pin_1
  N4: U1.Q4, R4.Pin_1
  N5: U1.Q5, R5.Pin_1
  N6: U1.Q6, R6.Pin_1
  N7: U1.Q7, R7.Pin_1
  GND: U1.GND, U1.OE, U2.GND, U2.OE, J1.pin1, U3.GND, U3.OE, U4.GND, U4.OE, J2.pin1, J3.pin1, J4.pin1, J5.pin1
  N8: U1.Q7', U2.DS
  VCC: U1.MR, U1.VCC, J1.pin5, U3.MR, U3.VCC, U4.MR, U4.VCC
  N9: U1.SH_CP, J1.pin4, U3.SH_CP, U4.SH_CP
  N10: U1.ST_CP, U2.ST_CP, J1.pin3, U3.ST_CP, U4.ST_CP
  N11: U1.DS, J1.pin2
  N12: U1.Q0, R8.Pin_1
  N13: R1.Pin_0, J2.pin3
  N14: R2.Pin_0, J2.pin4
  N15: R3.Pin_0, J2.pin5
  N16: R4.Pin_0, J2.pin6
  N17: R5.Pin_0, J2.pin7
  N18: R6.Pin_0, J2.pin8
  N19: R7.Pin_0, J2.pin9
  N20: R8.Pin_0, J2.pin2
  N21: U2.Q1, R10.Pin_1
  N22: U2.Q2, R11.Pin_1
  N23: U2.Q3, R12.Pin_1
  N24: U2.Q4, R13.Pin_1
  N25: U2.Q5, R14.Pin_1
  N26: U2.Q6, R15.Pin_1
  N27: U2.Q7, R16.Pin_1
  N28: U2.Q7', U3.DS
  N29: U2.Q0, R9.Pin_1
  N30: R9.Pin_0, J3.pin2
  N31: R10.Pin_0, J3.pin3
  N32: R11.Pin_0, J3.pin4
  N33: R12.Pin_0, J3.pin5
  N34: R13.Pin_0, J3.pin6
  N35: R14.Pin_0, J3.pin7
  N36: R15.Pin_0, J3.pin8
  N37: R16.Pin_0, J3.pin9
  N38: U3.Q1, R18.Pin_1
  N39: U3.Q2, R19.Pin_1
  N40: U3.Q3, R20.Pin_1
  N41: U3.Q4, R21.Pin_1
  N42: U3.Q5, R22.Pin_1
  N43: U3.Q6, R23.Pin_1
  N44: U3.Q7, R24.Pin_1
  N45: U3.Q7', U4.DS
  N46: U3.Q0, R17.Pin_1
  N47: R17.Pin_0, J4.pin2
  N48: R18.Pin_0, J4.pin3
  N49: R19.Pin_0, J4.pin4
  N50: R20.Pin_0, J4.pin5
  N51: R21.Pin_0, J4.pin6
  N52: R22.Pin_0, J4.pin7
  N53: R23.Pin_0, J4.pin8
  N54: R24.Pin_0, J4.pin9
  N55: U4.Q1, R26.Pin_1
  N56: U4.Q2, R27.Pin_1
  N57: U4.Q3, R28.Pin_1
  N58: U4.Q4, R29.Pin_1
  N59: U4.Q5, R30.Pin_1
  N60: U4.Q6, R31.Pin_1
  N61: U4.Q7, R32.Pin_1
  N62: U4.Q0, R25.Pin_1
  N63: R25.Pin_0, J5.pin2
  N64: R26.Pin_0, J5.pin3
  N65: R27.Pin_0, J5.pin4
  N66: R28.Pin_0, J5.pin5
  N67: R29.Pin_0, J5.pin6
  N68: R30.Pin_0, J5.pin7
  N69: R31.Pin_0, J5.pin8
  N70: R32.Pin_0, J5.pin9
