# Fritzing sketch heading (saved by Fritzing 0.9.3b)
circuit board: 10.1511cm x 6.78299cm
breadboards: 1

parts:
  U1 = 74HC595 [package="DIP16 [THT]"]
  U2 = 74HC595 [package="DIP16 [THT]"]
  U3 = 74HC595 [package="DIP16 [THT]"]
  R1 = Resistor [tolerance=±5% resistance=220 package=THT]
  R2 = Resistor [tolerance=±5% resistance=220 package=THT]
  R3 = Resistor [tolerance=±5% resistance=220 package=THT]
  R4 = Resistor [tolerance=±5% resistance=220 package=THT]
  R5 = Resistor [tolerance=±5% resistance=220 package=THT]
  R6 = Resistor [tolerance=±5% resistance=220 package=THT]
  R7 = Resistor [tolerance=±5% resistance=220 package=THT]
  R8 = Resistor [tolerance=±5% resistance=220 package=THT]
  R9 = Resistor [tolerance=±5% resistance=220 package=THT]
  R10 = Resistor [tolerance=±5% resistance=220 package=THT]
  R11 = Resistor [tolerance=±5% resistance=220 package=THT]
  R12 = Resistor [tolerance=±5% resistance=220 package=THT]
  R13 = Resistor [tolerance=±5% resistance=220 package=THT]
  R14 = Resistor [tolerance=±5% resistance=220 package=THT]
  R15 = Resistor [tolerance=±5% resistance=220 package=THT]
  R16 = Resistor [tolerance=±5% resistance=220 package=THT]
  R17 = Resistor [tolerance=±5% resistance=220 package=THT]
  R18 = Resistor [tolerance=±5% resistance=220 package=THT]
  R19 = Resistor [tolerance=±5% resistance=220 package=THT]
  R20 = Resistor [tolerance=±5% resistance=220 package=THT]
  R21 = Resistor [tolerance=±5% resistance=220 package=THT]
  R22 = Resistor [tolerance=±5% resistance=220 package=THT]
  R23 = Resistor [tolerance=±5% resistance=220 package=THT]
  R24 = Resistor [tolerance=±5% resistance=220 package=THT]
  J1 = female pin header, 2 pins [form="♀ (female)"]
  J2 = female pin header, 2 pins [form="♀ (female)"]
  J3 = female pin header, 2 pins [form="♀ (female)"]
  7_Segment1 = 7 Segment Display
  7_Segment2 = 7 Segment Display
  7_Segment3 = 7 Segment Display
  HDG_Rotary_Encoder = Rotary Encoder [package=THT]
  HDG_SELECT_BTN = Pushbutton [package=THT]
  J4 = female pin header, 2 pins [form="♀ (female)"]
  J5 = female pin header, 2 pins [form="♀ (female)"]
  HDG_HOLD_BTN = Pushbutton [package=THT]
  HDG_HOLD_LED = LED - 5mm [color="Red (633nm)" package="5 mm [THT]"]
  HDG_HOLD_LED1 = LED - 5mm [color="Red (633nm)" package="5 mm [THT]"]
  R25 = Resistor [tolerance=±5% resistance=220 package=THT]
  R26 = Resistor [tolerance=±5% resistance=220 package=THT]

nets:
  N1: U1.Q1, R2.Pin_1
  N2: U1.Q2, R3.Pin_1
  N3: U1.Q3, R4.Pin_1
  N4: U1.Q4, R5.Pin_1
  N5: U1.Q5, R6.Pin_1
  N6: U1.Q6, R7.Pin_1
  N7: U1.Q7, R8.Pin_1
  GND: U1.GND, U2.GND, U3.GND, 7_Segment1.common_cathode, 7_Segment2.common_cathode, 7_Segment3.common_cathode, HDG_Rotary_Encoder.EncoderPinC, HDG_SELECT_BTN.leg0, HDG_HOLD_BTN.leg0, HDG_HOLD_LED.cathode, HDG_HOLD_LED1.cathode
  N8: U1.Q7', U2.DS
  N9: U1.MR, U2.MR, U3.MR, J3.pin1
  N10: U1.SH_CP, U2.SH_CP, U3.SH_CP, J2.pin2
  N11: U1.ST_CP, U2.ST_CP, U3.ST_CP, J2.pin1
  N12: U1.OE, U2.OE, U3.OE, J1.pin2
  N13: U1.DS, J1.pin1
  N14: U1.Q0, R1.Pin_1
  5V: U1.VCC, U2.VCC, U3.VCC
  N15: U2.Q1, R11.Pin_1
  N16: U2.Q2, R12.Pin_1
  N17: U2.Q3, R15.Pin_1
  N18: U2.Q4, R13.Pin_1
  N19: U2.Q5, R16.Pin_1
  N20: U2.Q6, R9.Pin_1
  N21: U2.Q7, R14.Pin_1
  N22: U2.Q7', U3.DS
  N23: U2.Q0, R10.Pin_1
  N24: U3.Q1, R19.Pin_1
  N25: U3.Q2, R20.Pin_1
  N26: U3.Q3, R23.Pin_1
  N27: U3.Q4, R21.Pin_1
  N28: U3.Q5, R24.Pin_1
  N29: U3.Q6, R17.Pin_1
  N30: U3.Q7, R22.Pin_1
  N31: U3.Q0, R18.Pin_1
  N32: R1.Pin_0, 7_Segment1.Segment_A#10
  N33: R2.Pin_0, 7_Segment1.Segment_B
  N34: R3.Pin_0, 7_Segment1.Segment_C
  N35: R4.Pin_0, 7_Segment1.Segment_D
  N36: R5.Pin_0, 7_Segment1.Segment_E
  N37: R6.Pin_0, 7_Segment1.Segment_F
  N38: R7.Pin_0, 7_Segment1.Segment_A#1
  N39: R8.Pin_0, 7_Segment1.Segment_DP
  N40: R9.Pin_0, 7_Segment2.Segment_A#1
  N41: R10.Pin_0, 7_Segment2.Segment_A#10
  N42: R11.Pin_0, 7_Segment2.Segment_B
  N43: R12.Pin_0, 7_Segment2.Segment_C
  N44: R13.Pin_0, 7_Segment2.Segment_E
  N45: R14.Pin_0, 7_Segment2.Segment_DP
  N46: R15.Pin_0, 7_Segment2.Segment_D
  N47: R16.Pin_0, 7_Segment2.Segment_F
  N48: R17.Pin_0, 7_Segment3.Segment_A#1
  N49: R18.Pin_0, 7_Segment3.Segment_A#10
  N50: R19.Pin_0, 7_Segment3.Segment_B
  N51: R20.Pin_0, 7_Segment3.Segment_C
  N52: R21.Pin_0, 7_Segment3.Segment_E
  N53: R22.Pin_0, 7_Segment3.Segment_DP
  N54: R23.Pin_0, 7_Segment3.Segment_D
  N55: R24.Pin_0, 7_Segment3.Segment_F
  N56: J3.pin2, HDG_Rotary_Encoder.EncoderPinA
  N57: HDG_Rotary_Encoder.EncoderPinB, J4.pin1
  N58: HDG_SELECT_BTN.leg1, J4.pin2
  N59: J5.pin1, HDG_HOLD_BTN.leg1
  N60: J5.pin2, R25.Pin_1, R26.Pin_1
  N61: HDG_HOLD_LED.anode, R25.Pin_0
  N62: HDG_HOLD_LED1.anode, R26.Pin_0

notes:
  HDG_DISPLAY_SER
  SR_OUTPUT_ENABLE_PIN
  SR_LATCH_PIN
  SR_CLOCK_PIN
  SR_CLEAR_PIN
  HDG_DEG_A_PIN
  HDG_DEG_B_PIN
  HDG_SELECT_PIN
  HDG_HOLD_BTN_PIN
  HDG_HOLD_LED_PIN
